// Logisim project ALU.circ as structural Verilog: 6 circuits, main circuit main
module main (
  input  [3:0] A,
  input  [3:0] B,
  input  [1:0] in_3,
  output [3:0] \output 
);

  wire [3:0] add_1_add_output, and_1_output, not_1_out, not_2_out, not_3_out, or_1_output, xor_1_output;

  AND and_1 (.A(A), .B(B), .\output (and_1_output));
  OR or_1 (.A(A), .B(B), .\output (or_1_output));
  XOR xor_1 (.A(A), .B(B), .\output (xor_1_output));
  ADD add_1 (.Sel(1'b0), .B(B), .A(A), .add_output(add_1_add_output));  // open: Carry_out
  assign not_1_out = ~and_1_output;  // NOT_Gate not_1, 4 bits wide
  assign not_2_out = ~or_1_output;  // NOT_Gate not_2, 4 bits wide
  assign not_3_out = ~xor_1_output;  // NOT_Gate not_3, 4 bits wide
  Multiplexer #(.select(2), .width(4)) multiplexer_1 (
    .in0(not_1_out), .in1(not_2_out), .in2(not_3_out), .in3(add_1_add_output), .out(\output ), .sel(in_3));  // open: en
  Hex_Digit_Display hex_digit_display_1 (.value(\output ));  // open: dp

  // Notes on the sheet:
  //   1701CS21
  //   00: NAND 
  //   01: NOR
  //   10: XNOR
  //   11: ADD
endmodule

module AND (
  input  [3:0] A,
  input  [3:0] B,
  output [3:0] \output 
);

  and and_1 (\output [0], A[0], B[0]);
  and and_2 (\output [1], A[1], B[1]);
  and and_3 (\output [2], A[2], B[2]);
  and and_4 (\output [3], A[3], B[3]);
endmodule

module OR (
  input  [3:0] A,
  input  [3:0] B,
  output [3:0] \output 
);

  or or_1 (\output [0], A[0], B[0]);
  or or_2 (\output [1], A[1], B[1]);
  or or_3 (\output [2], A[2], B[2]);
  or or_4 (\output [3], A[3], B[3]);
endmodule

module XOR (
  input  [3:0] A,
  input  [3:0] B,
  output [3:0] \output 
);

  xor xor_1 (\output [0], A[0], B[0]);
  xor xor_2 (\output [1], A[1], B[1]);
  xor xor_3 (\output [2], A[2], B[2]);
  xor xor_4 (\output [3], A[3], B[3]);
endmodule

module FA (
  input  A,
  input  B,
  input  Cin,
  output sum_output,
  output Carry_out
);

  wire and_1_out, and_2_out, xor_1_out;

  xor xor_1 (xor_1_out, A, B);
  xor xor_2 (sum_output, xor_1_out, Cin);
  and and_1 (and_1_out, Cin, xor_1_out);
  and and_2 (and_2_out, A, B);
  or or_1 (Carry_out, and_1_out, and_2_out);
endmodule

module ADD (
  input  Sel,
  input  [3:0] B,
  input  [3:0] A,
  output [3:0] add_output,
  output Carry_out
);

  wire fa_1_carry_out, fa_2_carry_out, fa_3_carry_out, xor_1_out, xor_2_out, xor_3_out, xor_4_out;

  xor xor_1 (xor_1_out, B[0], Sel);
  FA fa_1 (.A(A[0]), .B(xor_1_out), .Cin(Sel), .sum_output(add_output[0]), .Carry_out(fa_1_carry_out));
  xor xor_2 (xor_2_out, B[1], Sel);
  FA fa_2 (.A(A[1]), .B(xor_2_out), .Cin(fa_1_carry_out), .sum_output(add_output[1]), .Carry_out(fa_2_carry_out));
  xor xor_3 (xor_3_out, B[2], Sel);
  xor xor_4 (xor_4_out, B[3], Sel);
  FA fa_3 (.A(A[2]), .B(xor_3_out), .Cin(fa_2_carry_out), .sum_output(add_output[2]), .Carry_out(fa_3_carry_out));
  FA fa_4 (.A(A[3]), .B(xor_4_out), .Cin(fa_3_carry_out), .sum_output(add_output[3]), .Carry_out(Carry_out));
endmodule
