// Logisim project sequence detector.circ as structural Verilog: 1 circuit, main circuit main
module main (
  input  clear,
  input  enable,
  input  input___x,
  output q2,
  output q1,
  output q0,
  output \output 
);

  wire and_1_out, and_2_out, and_3_out, and_4_out, and_5_out, and_6_out, and_7_out, and_8_out, and_9_out,
       and_10_out, and_11_out, and_12_out, and_13_out, and_14_out, clock_out, not_1_out, not_2_out,
       not_3_out, not_4_out, or_1_out, or_2_out, or_3_out;

  not not_1 (not_1_out, input___x);
  and and_1 (and_1_out, not_2_out, q2);
  and and_2 (and_2_out, input___x, q2);
  and and_3 (and_3_out, q1, not_1_out);
  and and_4 (and_4_out, input___x, not_3_out, not_2_out);
  and and_5 (and_5_out, not_4_out, not_3_out, q0, input___x);
  and and_6 (and_6_out, not_1_out, q1);
  and and_7 (and_7_out, not_1_out, q2, not_2_out);
  and and_8 (and_8_out, q1, not_2_out);
  and and_9 (and_9_out, q2, input___x);
  and and_10 (and_10_out, q0, q1, input___x);
  and and_11 (and_11_out, q1, not_1_out);
  and and_12 (and_12_out, q2, input___x);
  and and_13 (and_13_out, not_2_out, q2);
  and and_14 (and_14_out, q1, q0);
  or or_1 (or_1_out, and_1_out, and_2_out, and_3_out, and_4_out);
  or or_2 (or_2_out, and_5_out, and_6_out, and_7_out, and_8_out);
  or or_3 (or_3_out, and_9_out, and_10_out);
  not not_2 (not_2_out, q0);
  or or_4 (\output , and_11_out, and_12_out, and_13_out, and_14_out);
  not not_3 (not_3_out, q1);
  D_Flip_Flop d_ff_1 (.clk(clock_out), .D(or_1_out), .Q(q0), .en(enable), .reset(clear));  // open: Qn, preset
  D_Flip_Flop d_ff_2 (.clk(clock_out), .D(or_2_out), .Q(q1), .en(enable), .reset(clear));  // open: Qn, preset
  D_Flip_Flop d_ff_3 (.clk(clock_out), .D(or_3_out), .Q(q2), .en(enable), .reset(clear));  // open: Qn, preset
  not not_4 (not_4_out, q2);
  Clock clock (.out(clock_out));
  Hex_Digit_Display hex_digit_display_1 (.value({1'b0, q2, q1, q0}));  // open: dp

  // Notes on the sheet:
  //   1701CS21
endmodule
